// Logisim project Cache.circ as structural Verilog: 13 circuits, main circuit main
module main (
  input  EnableTestHalting,
  input  Valid0,
  output [9:0] CorrectCounter,
  output [9:0] HitCounter,
  output [9:0] MissCounter,
  output [9:0] TestNumber,
  output [7:0] ByteRead,
  output [7:0] CorrectByteRead,
  output Halt
);

  wire and_3_out, and_4_out, and_5_out, CLK, CmdIsRead, Correct, CpuRead, CpuWrite, DidContain, HaltTesting,
       MaxItersReached, MemRead, MemWrite, not_1_out, not_2_out, not_4_out, NotDoneTesting, Ok2Count,
       or_1_out, Ready;
  wire [7:0] CpuWriteValue, MemAddress;
  wire [9:0] CpuAddress;
  wire [31:0] Line2Mem, LineFromMem;

  not not_1 (not_1_out, Ready);
  Clock clock_1 (.out(CLK));
  or or_1 (or_1_out, MaxItersReached, Ready);
  Counter #(.width(4), .max('h9)) MaxClocks (
    .load(Ready), .D(4'b0001), .count(not_1_out), .carry(MaxItersReached), .clk(CLK));  // open: Q, clr
  and and_1 (HaltTesting, EnableTestHalting, CmdIsRead, not_2_out);
  not not_2 (not_2_out, Correct);
  not not_3 (NotDoneTesting, Halt);
  Inputs inputs_1 (
    .HaltTesting(HaltTesting), .Ready(or_1_out), .CLK(CLK), .Done(Halt), .Read(CpuRead), .Write(CpuWrite),
    .Address(CpuAddress), .Value(CpuWriteValue), .TestNumber(TestNumber));
  Cache cache_1 (
    .CpuAddress(CpuAddress), .CpuRead(CpuRead), .CpuWrite(CpuWrite), .CpuWriteValue(CpuWriteValue),
    .CLK(CLK), .Ready(Ready), .DidContain(DidContain), .ByteRead(ByteRead), .MemAddress(MemAddress),
    .MemRead(MemRead), .MemWrite(MemWrite), .LineFromMem(LineFromMem), .Line2Mem(Line2Mem));
  // Probe on CpuRead
  // Probe on CpuWrite
  // Probe on CpuAddress
  // Probe on CpuWriteValue
  // Probe on TestNumber
  // Probe on CorrectByteRead
  // Probe on Correct
  // Probe on Ready
  // Probe on DidContain
  // Probe on ByteRead
  // Probe on MemAddress
  // Probe on MemRead
  // Probe on MemWrite
  // Probe on HitCounter
  // Probe on LineFromMem
  // Probe on Line2Mem
  not not_4 (not_4_out, HaltTesting);
  RAM #(.dataWidth(32), .bus("separate")) ram_1 (
    .addr(MemAddress), .din(Line2Mem), .data(LineFromMem), .str(MemWrite), .clk(CLK), .ld(MemRead));  // open: sel, clr
  and and_2 (Ok2Count, Ready, not_4_out, NotDoneTesting);
  and and_3 (and_3_out, Correct, Ok2Count);
  and and_4 (and_4_out, DidContain, Ok2Count);
  and and_5 (and_5_out, MemRead, NotDoneTesting);
  Checker checker_1 (
    .TestNumber(TestNumber), .YourByteRead(ByteRead), .CmdIsRead(CmdIsRead),
    .CorrectByteRead(CorrectByteRead), .Correct(Correct));
  Counter #(.width(10), .max('h3ff)) u_CorrectCounter (
    .count(and_3_out), .Q(CorrectCounter), .clk(CLK));  // open: load, D, carry, clr
  Counter #(.width(10), .max('h3ff)) u_HitCounter (
    .count(and_4_out), .Q(HitCounter), .clk(CLK));  // open: load, D, carry, clr
  Counter #(.width(10), .max('h3ff)) u_MissCounter (
    .count(and_5_out), .Q(MissCounter), .clk(CLK));  // open: load, D, carry, clr
  // Probe on CorrectCounter
  // Probe on HitCounter
  // Probe on MissCounter

  // Other names for the same wires on the sheet: DoneTesting = Halt

  // Notes on the sheet:
  //   Your Answer Inside Here
  //   Sairamvinay Vijayaraghavan - 913603345
  //   Hariharan Sezhiyan  - 913644281
endmodule

module Cache (
  input  [9:0] CpuAddress,
  input  CpuRead,
  input  CpuWrite,
  input  [7:0] CpuWriteValue,
  input  CLK,
  input  [31:0] LineFromMem,
  output Ready,
  output DidContain,
  output [7:0] ByteRead,
  output [7:0] MemAddress,
  output MemRead,
  output MemWrite,
  output [31:0] Line2Mem
);

  wire DidContain0, DidContain1, MemRead0, MemRead1, MemWrite0, MemWrite1, SavedRead, SavedWrite,
       selectcvd_1_contains, selectcvd_1_dirty, selectcvd_1_valid, set_1_contains, set_1_dirty, set_1_valid,
       set_2_contains, set_2_dirty, set_2_valid, setselect_1_s0_0, setselect_1_s0_1, setselect_1_s1_0,
       setselect_1_s1_1, setselect_1_s2_0, setselect_1_s2_1, Start, xor_1_out;
  wire [1:0] offSet;
  wire [2:0] nextstate_1_s0p, State_5_q;
  wire [7:0] ByteRead0, ByteRead1, WriteVal;
  wire [31:0] Line2Mem0, Line2Mem1;

  Register #(.width(10)) State (.D(CpuAddress), .en(Start), .Q({MemAddress, offSet}), .clk(CLK));  // open: clr
  Register #(.width(1)) State_2 (.D(CpuRead), .en(Start), .Q(SavedRead), .clk(CLK));  // open: clr
  Register #(.width(1)) State_3 (.D(CpuWrite), .en(Start), .Q(SavedWrite), .clk(CLK));  // open: clr
  Register State_4 (.D(CpuWriteValue), .en(Start), .Q(WriteVal), .clk(CLK));  // open: clr
  xor xor_1 (xor_1_out, CpuRead, CpuWrite);
  and and_1 (Start, Ready, xor_1_out);
  SetSelect setselect_1 (
    .S2(State_5_q[2]), .S1(State_5_q[1]), .S0(State_5_q[0]), .Set(MemAddress[0]), .S2_0(setselect_1_s2_0),
    .S1_0(setselect_1_s1_0), .S0_0(setselect_1_s0_0), .S2_1(setselect_1_s2_1), .S1_1(setselect_1_s1_1),
    .S0_1(setselect_1_s0_1));
  Set set_1 (
    .S2(setselect_1_s2_0), .S1(setselect_1_s1_0), .S0(setselect_1_s0_0), .Tag(MemAddress[7:1]),
    .Offset(offSet), .CpuRead(SavedRead), .CpuWrite(SavedWrite), .CpuWriteValue(WriteVal),
    .LineFromMem(LineFromMem), .Clock(CLK), .Contains(set_1_contains), .Valid(set_1_valid),
    .Dirty(set_1_dirty), .MemRead(MemRead0), .MemWrite(MemWrite0), .Line2Mem(Line2Mem0),
    .ByteRead(ByteRead0), .DidContain(DidContain0));
  Set set_2 (
    .S2(setselect_1_s2_1), .S1(setselect_1_s1_1), .S0(setselect_1_s0_1), .Tag(MemAddress[7:1]),
    .Offset(offSet), .CpuRead(SavedRead), .CpuWrite(SavedWrite), .CpuWriteValue(WriteVal),
    .LineFromMem(LineFromMem), .Clock(CLK), .Contains(set_2_contains), .Valid(set_2_valid),
    .Dirty(set_2_dirty), .MemRead(MemRead1), .MemWrite(MemWrite1), .Line2Mem(Line2Mem1),
    .ByteRead(ByteRead1), .DidContain(DidContain1));
  SelectCVD selectcvd_1 (
    .C0(set_1_contains), .V0(set_1_valid), .D0(set_1_dirty), .C1(set_2_contains), .V1(set_2_valid),
    .D1(set_2_dirty), .Set(MemAddress[0]), .Contains(selectcvd_1_contains), .Valid(selectcvd_1_valid),
    .Dirty(selectcvd_1_dirty));
  NextState nextstate_1 (
    .S2(State_5_q[2]), .S1(State_5_q[1]), .S0(State_5_q[0]), .C(selectcvd_1_contains), .V(selectcvd_1_valid),
    .D(selectcvd_1_dirty), .R(SavedRead), .W(SavedWrite), .S2p(nextstate_1_s0p[2]), .S1p(nextstate_1_s0p[1]),
    .S0p(nextstate_1_s0p[0]), .Ready(Ready));
  Register #(.width(3)) State_5 (.D(nextstate_1_s0p), .Q(State_5_q), .clk(CLK));  // open: en, clr
  Multiplexer #(.enable("false")) multiplexer_1 (.in0(MemRead0), .in1(MemRead1), .out(MemRead), .sel(MemAddress[0]));
  Multiplexer #(.enable("false")) multiplexer_2 (.in0(MemWrite0), .in1(MemWrite1), .out(MemWrite), .sel(MemAddress[0]));
  Multiplexer #(.width(32), .enable("false")) multiplexer_3 (
    .in0(Line2Mem0), .in1(Line2Mem1), .out(Line2Mem), .sel(MemAddress[0]));
  Multiplexer #(.width(8), .enable("false")) multiplexer_4 (
    .in0(ByteRead0), .in1(ByteRead1), .out(ByteRead), .sel(MemAddress[0]));
  Multiplexer #(.enable("false")) multiplexer_5 (
    .in0(DidContain0), .in1(DidContain1), .out(DidContain), .sel(MemAddress[0]));

  // Other names for the same wires on the sheet: Set = MemAddress[0]; Tag[6:0] = MemAddress[7:1]

  // Notes on the sheet:
  //   Address Bits = 10
  //   Line Size = 4
  //   W = 3
  //   Num Sets = 2
  //   C =4*3*2 = 24bytes
  //   Tag bits = 7
  //   Set 0
  //   Set 1
endmodule

module Inputs (
  input  HaltTesting,
  input  Ready,
  input  CLK,
  output Done,
  output Read,
  output Write,
  output [9:0] Address,
  output [7:0] Value,
  output [9:0] TestNumber
);

  wire and_1_out, not_1_out, not_2_out;

  not not_1 (not_1_out, HaltTesting);
  not not_2 (not_2_out, Done);
  Counter #(.width(10), .max('h3ff), .ongoal("stay")) u_TestNumber (
    .count(and_1_out), .Q(TestNumber), .clk(CLK));  // open: load, D, carry, clr
  and and_1 (and_1_out, not_1_out, Ready, not_2_out);
  ROM #(.addrWidth(10), .dataWidth(21)) rom_1 (
    .addr(TestNumber), .data({Done, Read, Write, Address, Value}));  // open: sel

  // Notes on the sheet:
  //   contents of rom_1 (hex, n*v repeats v):
  //   80882 83fe6 4306b 83e0e 43701 42275 8280f 80304 41bd8 84371 43f77 41d70 4250b 44733 8253d 440d8
  //   82691 440c9 83d7c 43558 446bf 83837 842c9 43e0f 4059d 41556 80166 833b0 43a89 83142 8361c 42e66
  //   43eb6 42c00 43a0e 8165c 84682 8092a 83907 41f89 817b0 40855 82056 425e8 43ff2 8039f 42bd7 82137
  //   4416b 40273 8324a 814e4 44570 41c0f 429da 82640 8069c 8099e 414d5 41004 81beb 84113 419b1 81add
  //   83f35 425ff 829cd 40250 82945 4366d 40cc2 444f8 80814 81156 8446d 42a82 42bae 82578 41135 405d0
  //   8304b 82b3a 40972 822ba 4443a 42337 82506 80bd3 80560 83552 83955 81434 43096 43da1 81aa2 80305
  //   428e6 428cc 808a2 40e80 845f0 4215d 82765 82e29 40be5 82b74 42715 417a2 41fab 8452f 81c0a 83325
  //   44624 80205 42dfc 41333 40958 81348 42736 41069 84510 44669 826dd 8067e 408e4 44680 444e8 832ad
  //   821f8 83509 82d46 81184 432cd 80b77 4005a 440e0 81ea0 43d73 42b8c 80624 41468 42699 415ed 80fc1 0
  //   100000
endmodule

module Checker (
  input  [9:0] TestNumber,
  input  [7:0] YourByteRead,
  output CmdIsRead,
  output [7:0] CorrectByteRead,
  output Correct
);

  wire comparator_1_eq;
  wire [9:0] subtractor_1_out;

  // Probe on TestNumber
  Subtractor #(.width(10)) subtractor_1 (.a(TestNumber), .b(10'h1), .out(subtractor_1_out));  // open: bin, bout
  ROM #(.addrWidth(10), .dataWidth(9)) rom_1 (
    .addr(subtractor_1_out), .data({CmdIsRead, CorrectByteRead}));  // open: sel
  Comparator #(.mode("unsigned")) comparator_1 (
    .a(YourByteRead), .b(CorrectByteRead), .eq(comparator_1_eq));  // open: gt, lt
  and and_1 (Correct, comparator_1_eq, CmdIsRead);

  // Other names for the same wires on the sheet: Test_Number[9:0] = TestNumber

  // Notes on the sheet:
  //   Read Solutions
  //   contents of rom_1 (hex, n*v repeats v):
  //   1a3 1dc 6b 125 1 75 1dc 1c3 d8 1ab 77 70 b 33 10b d8 1c3 c9 174 58 bf 153 199 f 9d 56 1bb 13b 89 16c
  //   180 66 b6 0 e 107 1bf 1d8 167 89 118 55 1a2 e8 f2 1c3 d7 142 6b 73 1ab 18c 70 f da 1c3 14c 1d8 d5 4
  //   1d8 16b b1 1f4 1f2 ff 1da 50 1da 6d c2 f8 155 1c6 1f8 82 ae 1ff 35 d0 16b 1ae 72 175 3a 37 1ff 173
  //   1d0 158 167 1d5 96 a1 1f4 1c3 e6 cc 155 80 170 5d 1e6 166 e5 1ae 15 a2 ab 170 10f 13b 24 150 fc 33
  //   58 133 36 69 170 69 1c3 14c e4 80 e8 1ab 15d 158 1fc 135 cd 1e5 5a e0 104 73 8c 14c 68 99 ed 1a6
endmodule

module Set (
  input  S2,
  input  S1,
  input  S0,
  input  [6:0] Tag,
  input  [1:0] Offset,
  input  CpuRead,
  input  CpuWrite,
  input  [7:0] CpuWriteValue,
  input  [31:0] LineFromMem,
  input  Clock,
  output Contains,
  output Valid,
  output Dirty,
  output MemRead,
  output MemWrite,
  output [31:0] Line2Mem,
  output [7:0] ByteRead,
  output DidContain
);

  wire and_1_out, and_2_out, ChooseEvict, chooseoutputsignals_1_readfrommem_2,
       chooseoutputsignals_1_readfrommem_3, chooseoutputsignals_1_readfrommem_4,
       chooseoutputsignals_1_readreturn_2, chooseoutputsignals_1_readreturn_3,
       chooseoutputsignals_1_readreturn_4, chooseoutputsignals_1_writereturn_2,
       chooseoutputsignals_1_writereturn_3, chooseoutputsignals_1_writereturn_4,
       chooseoutputsignals_1_writetomem_2, chooseoutputsignals_1_writetomem_3,
       chooseoutputsignals_1_writetomem_4, contains0, contains1, contains2, dirty0, dirty1, dirty2, Init,
       not_1_out, not_2_out, or_1_out, ReadFromMem, ReadReturn, Start, UpdateAges, valid0, valid1, valid2,
       WriteReturn, WriteToMem;
  wire [1:0] age0, age1, age2, chooseblock_1_selected_set, chooseevict_1_linetoevict, multiplexer_1_out,
       selectedAge, SelectedBlockContains, SelectedBlockEvict, StoredSelectedBlock;
  wire [7:0] ByteRead0, ByteRead1, ByteRead2;
  wire [31:0] line0, line1, line2, Line2Mem_t, multiplexer_5_out;

  Demultiplexer #(.select(3), .enable("false")) demultiplexer_1 (
    .out0(Init), .out1(Start), .out2(ChooseEvict), .out3(WriteToMem), .out4(ReadFromMem), .out5(UpdateAges),
    .out6(ReadReturn), .out7(WriteReturn), .in(1'b1), .sel({S2, S1, S0}));
  Multiplexer #(.width(2), .enable("false")) multiplexer_1 (
    .in0(SelectedBlockContains), .in1(SelectedBlockEvict), .out(multiplexer_1_out), .sel(ChooseEvict));
  or or_1 (or_1_out, ChooseEvict, and_1_out);
  and and_1 (and_1_out, UpdateAges, DidContain);
  Register #(.width(32)) State (.D(Line2Mem_t), .Q(Line2Mem), .clk(Clock));  // open: en, clr
  Register #(.width(1)) State_2 (.D(Contains), .en(Start), .Q(DidContain), .clk(Clock));  // open: clr
  Register #(.width(2)) State_3 (
    .D(multiplexer_1_out), .en(or_1_out), .Q(StoredSelectedBlock), .clk(Clock));  // open: clr
  Multiplexer #(.select(2), .width(2), .enable("false")) multiplexer_2 (
    .in0(age0), .in1(age1), .in2(age2), .in3(2'b00), .out(selectedAge), .sel(StoredSelectedBlock));
  ChooseOutputSignals chooseoutputsignals_1 (
    .ReadFromMem(ReadFromMem), .ReadReturn(ReadReturn), .WriteReturn(WriteReturn), .WriteToMem(WriteToMem),
    .SelectedBlock(StoredSelectedBlock), .ReadFromMem_2(chooseoutputsignals_1_readfrommem_2),
    .ReadReturn_2(chooseoutputsignals_1_readreturn_2), .WriteReturn_2(chooseoutputsignals_1_writereturn_2),
    .WriteToMem_2(chooseoutputsignals_1_writetomem_2), .ReadFromMem_3(chooseoutputsignals_1_readfrommem_3),
    .ReadReturn_3(chooseoutputsignals_1_readreturn_3), .WriteReturn_3(chooseoutputsignals_1_writereturn_3),
    .WriteToMem_3(chooseoutputsignals_1_writetomem_3), .ReadFromMem_4(chooseoutputsignals_1_readfrommem_4),
    .ReadReturn_4(chooseoutputsignals_1_readreturn_4), .WriteReturn_4(chooseoutputsignals_1_writereturn_4),
    .WriteToMem_4(chooseoutputsignals_1_writetomem_4));
  or or_2 (Contains, contains0, contains1, contains2);
  Multiplexer #(.select(2), .enable("false")) multiplexer_3 (
    .in0(valid0), .in1(valid1), .in2(valid2), .in3(1'b0), .out(Valid), .sel(StoredSelectedBlock));
  Multiplexer #(.select(2), .enable("false")) multiplexer_4 (
    .in0(dirty0), .in1(dirty1), .in2(dirty2), .in3(1'b0), .out(Dirty), .sel(StoredSelectedBlock));
  Demultiplexer #(.width(2), .enable("false")) demultiplexer_2 (
    .out1(SelectedBlockContains), .in(chooseblock_1_selected_set), .sel(and_2_out));  // open: out0
  ChooseBlock chooseblock_1 (
    .Tag0(contains0), .Tag1(contains1), .Tag2(contains2), .Selected_Set(chooseblock_1_selected_set));  // open: Evict_or_not
  and and_2 (and_2_out, UpdateAges, DidContain);
  Multiplexer #(.select(2), .width(32), .enable("false")) multiplexer_5 (
    .in0(line0), .in1(line1), .in2(line2), .out(multiplexer_5_out), .sel(StoredSelectedBlock));  // open: in3
  ChooseEvict chooseevict_1 (
    .Valid0(valid0), .Valid1(valid1), .Valid0_2(valid2), .Age0(age0), .Age1(age1), .Age2(age2),
    .LinetoEvict(chooseevict_1_linetoevict));
  Multiplexer #(.width(2), .enable("false")) multiplexer_6 (
    .in0(2'b00), .in1(chooseevict_1_linetoevict), .out(SelectedBlockEvict), .sel(ChooseEvict));
  Multiplexer #(.width(32), .enable("false")) multiplexer_7 (
    .in0({32{1'b0}}), .in1(multiplexer_5_out), .out(Line2Mem_t), .sel(WriteToMem));
  Block block_1 (
    .StartingState(Init), .in_2(2'b00), .CpuRead(CpuRead), .CpuWrite(CpuWrite), .Tag(Tag), .Offset(Offset),
    .ReadFromMem(chooseoutputsignals_1_readfrommem_2), .ReadReturn(chooseoutputsignals_1_readreturn_2),
    .WriteReturn(chooseoutputsignals_1_writereturn_2), .WriteToMem(chooseoutputsignals_1_writetomem_2),
    .CpuWriteValue(CpuWriteValue), .UpdateAges(UpdateAges), .SelectedAge(selectedAge),
    .LineFromMem(LineFromMem), .Clock(Clock), .contains(contains0), .validOutput(valid0),
    .dirtyOutput(dirty0), .newAge(age0), .ByteRead(ByteRead0), .Line2Mem(line0));
  Block block_2 (
    .StartingState(Init), .in_2(2'b01), .CpuRead(CpuRead), .CpuWrite(CpuWrite), .Tag(Tag), .Offset(Offset),
    .ReadFromMem(chooseoutputsignals_1_readfrommem_3), .ReadReturn(chooseoutputsignals_1_readreturn_3),
    .WriteReturn(chooseoutputsignals_1_writereturn_3), .WriteToMem(chooseoutputsignals_1_writetomem_3),
    .CpuWriteValue(CpuWriteValue), .UpdateAges(UpdateAges), .SelectedAge(selectedAge),
    .LineFromMem(LineFromMem), .Clock(Clock), .contains(contains1), .validOutput(valid1),
    .dirtyOutput(dirty1), .newAge(age1), .ByteRead(ByteRead1), .Line2Mem(line1));
  Block block_3 (
    .StartingState(Init), .in_2(2'b10), .CpuRead(CpuRead), .CpuWrite(CpuWrite), .Tag(Tag), .Offset(Offset),
    .ReadFromMem(chooseoutputsignals_1_readfrommem_4), .ReadReturn(chooseoutputsignals_1_readreturn_4),
    .WriteReturn(chooseoutputsignals_1_writereturn_4), .WriteToMem(chooseoutputsignals_1_writetomem_4),
    .CpuWriteValue(CpuWriteValue), .UpdateAges(UpdateAges), .SelectedAge(selectedAge),
    .LineFromMem(LineFromMem), .Clock(Clock), .contains(contains2), .validOutput(valid2),
    .dirtyOutput(dirty2), .newAge(age2), .ByteRead(ByteRead2), .Line2Mem(line2));
  not not_1 (not_1_out, UpdateAges);
  not not_2 (not_2_out, ReadFromMem);
  and and_3 (MemRead, ReadFromMem, not_1_out);
  and and_4 (MemWrite, WriteToMem, not_2_out);
  Multiplexer #(.select(2), .width(8), .enable("false")) multiplexer_8 (
    .in0(ByteRead0), .in1(ByteRead1), .in2(ByteRead2), .out(ByteRead), .sel(StoredSelectedBlock));  // open: in3

  // Other names for the same wires on the sheet: CLK = Clock; StoredContains = DidContain;
  //   StoredWriteToMem[31:0] = Line2Mem
endmodule

module Block (
  input  StartingState,
  input  [1:0] in_2,
  input  CpuRead,
  input  CpuWrite,
  input  [6:0] Tag,
  input  [1:0] Offset,
  input  ReadFromMem,
  input  ReadReturn,
  input  WriteReturn,
  input  WriteToMem,
  input  [7:0] CpuWriteValue,
  input  UpdateAges,
  input  [1:0] SelectedAge,
  input  [31:0] LineFromMem,
  input  Clock,
  output contains,
  output validOutput,
  output dirtyOutput,
  output [1:0] newAge,
  output [7:0] ByteRead,
  output [31:0] Line2Mem
);

  wire comparator_1_eq, equals0, equals1, equals2, equals3, multiplexer_1_out, multiplexer_2_out,
       multiplexer_3_out, multiplexer_4_out, multiplexer_6_out, or_1_out, or_2_out, or_3_out, or_4_out,
       or_5_out, or_6_out, or_7_out, or_8_out, WriteReturn0, WriteReturn1, WriteReturn2, WriteReturn3;
  wire [1:0] multiplexer_5_out, updateages_1_newage;
  wire [6:0] storedBlockTag;
  wire [7:0] multiplexer_7_out, multiplexer_8_out, multiplexer_9_out, multiplexer_10_out, multiplexer_11_out,
       newVal0, newVal1, newVal2, newVal3;
  wire [31:0] Line2Mem_t;

  Multiplexer #(.enable("false")) multiplexer_1 (.in0(1'b0), .in1(1'b1), .out(multiplexer_1_out), .sel(WriteReturn));
  Multiplexer #(.enable("false")) multiplexer_2 (.in0(1'b0), .in1(1'b1), .out(multiplexer_2_out), .sel(ReadFromMem));
  updateAges updateages_1 (.selectedAge(SelectedAge), .Age(newAge), .NewAge(updateages_1_newage));
  or or_1 (or_1_out, UpdateAges, StartingState);
  Multiplexer #(.enable("false")) multiplexer_3 (
    .in0(multiplexer_2_out), .in1(1'b0), .out(multiplexer_3_out), .sel(StartingState));
  Multiplexer #(.enable("false")) multiplexer_4 (
    .in0(multiplexer_1_out), .in1(1'b0), .out(multiplexer_4_out), .sel(ReadFromMem));
  Multiplexer #(.width(2), .enable("false")) multiplexer_5 (
    .in0(updateages_1_newage), .in1(in_2), .out(multiplexer_5_out), .sel(StartingState));
  or or_2 (or_2_out, StartingState, ReadFromMem);
  Multiplexer #(.enable("false")) multiplexer_6 (
    .in0(multiplexer_4_out), .in1(1'b0), .out(multiplexer_6_out), .sel(StartingState));
  Register #(.width(2)) age (.D(multiplexer_5_out), .en(or_1_out), .Q(newAge), .clk(Clock));  // open: clr
  Register #(.width(1)) valid (.D(multiplexer_3_out), .en(or_2_out), .Q(validOutput), .clk(Clock));  // open: clr
  Register #(.width(1)) valid_2 (.D(multiplexer_6_out), .en(or_3_out), .Q(dirtyOutput), .clk(Clock));  // open: clr
  or or_3 (or_3_out, StartingState, WriteReturn, ReadFromMem);
  Multiplexer #(.width(8), .enable("false")) multiplexer_7 (
    .in0(CpuWriteValue), .in1(LineFromMem[7:0]), .out(multiplexer_7_out), .sel(ReadFromMem));
  or or_4 (or_4_out, ReadFromMem, WriteReturn0);
  Multiplexer #(.width(8), .enable("false")) multiplexer_8 (
    .in0(CpuWriteValue), .in1(LineFromMem[15:8]), .out(multiplexer_8_out), .sel(ReadFromMem));
  or or_5 (or_5_out, ReadFromMem, WriteReturn1);
  Multiplexer #(.width(8), .enable("false")) multiplexer_9 (
    .in0(CpuWriteValue), .in1(LineFromMem[31:24]), .out(multiplexer_9_out), .sel(ReadFromMem));
  Register Value_1 (.D(multiplexer_8_out), .en(or_5_out), .Q(newVal1), .clk(Clock));  // open: clr
  Multiplexer #(.width(8), .enable("false")) multiplexer_10 (
    .in0(CpuWriteValue), .in1(LineFromMem[23:16]), .out(multiplexer_10_out), .sel(ReadFromMem));
  or or_6 (or_6_out, ReadFromMem, WriteReturn2);
  or or_7 (or_7_out, ReadFromMem, WriteReturn3);
  Register Value_0 (.D(multiplexer_7_out), .en(or_4_out), .Q(newVal0), .clk(Clock));  // open: clr
  Register Value_2 (.D(multiplexer_10_out), .en(or_6_out), .Q(newVal2), .clk(Clock));  // open: clr
  Register Value_3 (.D(multiplexer_9_out), .en(or_7_out), .Q(newVal3), .clk(Clock));  // open: clr
  Comparator #(.width(7), .mode("unsigned")) comparator_1 (
    .a(storedBlockTag), .b(Tag), .eq(comparator_1_eq));  // open: gt, lt
  or or_8 (or_8_out, ReadReturn, WriteReturn);
  Multiplexer #(.select(2), .width(8), .enable("false")) multiplexer_11 (
    .in0(newVal0), .in1(newVal1), .in2(newVal2), .in3(newVal3), .out(multiplexer_11_out), .sel(Offset));
  Register #(.width(32)) State (
    .D({newVal3, newVal2, newVal1, newVal0}), .en(WriteToMem), .Q(Line2Mem_t), .clk(Clock));  // open: clr
  Register #(.width(7)) u_Tag (.D(Tag), .en(or_8_out), .Q(storedBlockTag), .clk(Clock));  // open: clr
  and and_1 (contains, comparator_1_eq, validOutput);
  Multiplexer #(.width(32), .enable("false")) multiplexer_12 (
    .in1(Line2Mem_t), .out(Line2Mem), .sel(WriteToMem));  // open: in0
  Comparator #(.width(2), .mode("unsigned")) comparator_2 (.a(2'b00), .b(Offset), .eq(equals0));  // open: gt, lt
  Comparator #(.width(2), .mode("unsigned")) comparator_3 (.a(2'b01), .b(Offset), .eq(equals1));  // open: gt, lt
  Comparator #(.width(2), .mode("unsigned")) comparator_4 (.a(2'b10), .b(Offset), .eq(equals2));  // open: gt, lt
  Comparator #(.width(2), .mode("unsigned")) comparator_5 (.a(2'b11), .b(Offset), .eq(equals3));  // open: gt, lt
  and and_2 (WriteReturn0, WriteReturn, equals0);
  and and_3 (WriteReturn1, WriteReturn, equals1);
  and and_4 (WriteReturn2, WriteReturn, equals2);
  and and_5 (WriteReturn3, WriteReturn, equals3);
  Multiplexer #(.width(8), .enable("false")) multiplexer_13 (
    .in0({8{1'b0}}), .in1(multiplexer_11_out), .out(ByteRead), .sel(ReadReturn));

  // Other names for the same wires on the sheet: Clk = Clock; Init = StartingState; InitAge[1:0] = in_2;
  //   storedAge[1:0] = newAge; storedDirty = dirtyOutput; storedValid = validOutput
endmodule

module ChooseEvict (
  input  Valid0,
  input  Valid1,
  input  Valid0_2,
  input  [1:0] Age0,
  input  [1:0] Age1,
  input  [1:0] Age2,
  output [1:0] LinetoEvict
);

  wire comparator_1_gt, comparator_6_gt, comparator_7_gt, comparator_8_gt, maximumage;
  wire [1:0] L2E, Linemax10, Linemax12, Linemax20, maxAge, multiplexer_1_out;
  wire [2:0] Line;

  Comparator #(.width(2), .mode("unsigned")) comparator_1 (.a(Age2), .b(Age1), .gt(comparator_1_gt));  // open: eq, lt
  Multiplexer #(.width(2), .enable("false")) multiplexer_1 (
    .in0(Age1), .in1(Age2), .out(multiplexer_1_out), .sel(comparator_1_gt));
  Comparator #(.width(2), .mode("unsigned")) comparator_2 (.a(maxAge), .b(Age0), .eq(Line[0]));  // open: gt, lt
  Comparator #(.width(2), .mode("unsigned")) comparator_3 (.a(maxAge), .b(Age1), .eq(Line[1]));  // open: gt, lt
  Comparator #(.width(2), .mode("unsigned")) comparator_4 (.a(maxAge), .b(Age2), .eq(Line[2]));  // open: gt, lt
  Multiplexer #(.select(3), .width(2), .enable("false")) multiplexer_2 (
    .in0(L2E), .in1(Linemax12), .in2(Linemax20), .in3(2'b10), .in4(Linemax10), .in5(2'b01), .in6(2'b00),
    .in7(L2E), .out(LinetoEvict), .sel({Valid0_2, Valid1, Valid0}));
  Multiplexer #(.width(2), .enable("false")) multiplexer_3 (
    .in0(Age0), .in1(multiplexer_1_out), .out(maxAge), .sel(maximumage));
  Comparator #(.width(2), .mode("unsigned")) comparator_5 (
    .a(multiplexer_1_out), .b(Age0), .gt(maximumage));  // open: eq, lt
  Multiplexer #(.select(3), .width(2), .enable("false")) multiplexer_4 (
    .in1(2'b00), .in2(2'b01), .in4(2'b10), .out(L2E), .sel(Line));  // open: in0, in3, in5, in6, in7
  Comparator #(.width(2), .mode("unsigned")) comparator_6 (.a(Age2), .b(Age1), .gt(comparator_6_gt));  // open: eq, lt
  Comparator #(.width(2), .mode("unsigned")) comparator_7 (.a(Age2), .b(Age0), .gt(comparator_7_gt));  // open: eq, lt
  Comparator #(.width(2), .mode("unsigned")) comparator_8 (.a(Age1), .b(Age0), .gt(comparator_8_gt));  // open: eq, lt
  Multiplexer #(.width(2), .enable("false")) multiplexer_5 (
    .in0(2'b01), .in1(2'b10), .out(Linemax12), .sel(comparator_6_gt));
  Multiplexer #(.width(2), .enable("false")) multiplexer_6 (
    .in0(2'b00), .in1(2'b10), .out(Linemax20), .sel(comparator_7_gt));
  Multiplexer #(.width(2), .enable("false")) multiplexer_7 (
    .in0(2'b00), .in1(2'b01), .out(Linemax10), .sel(comparator_8_gt));

  // Other names for the same wires on the sheet: ValidString[2:0] = {Valid0_2, Valid1, Valid0}; Valid2 = Valid0_2
endmodule

module updateAges (
  input  [1:0] selectedAge,
  input  [1:0] Age,
  output [1:0] NewAge
);

  wire equal, lessthan;
  wire [1:0] adder_1_out, multiplexer_1_out;

  Comparator #(.width(2), .mode("unsigned")) comparator_1 (
    .a(Age), .b(selectedAge), .eq(equal), .lt(lessthan));  // open: gt
  Multiplexer #(.width(2), .enable("false")) multiplexer_1 (
    .in0(Age), .in1(adder_1_out), .out(multiplexer_1_out), .sel(lessthan));
  Adder #(.width(2)) adder_1 (.a(Age), .b(2'b01), .out(adder_1_out));  // open: cin, cout
  Multiplexer #(.width(2), .enable("false")) multiplexer_2 (
    .in0(multiplexer_1_out), .in1(2'b00), .out(NewAge), .sel(equal));

  // Other names for the same wires on the sheet: BlockAge[1:0] = Age
endmodule

module ChooseBlock (
  input  Tag0,
  input  Tag1,
  input  Tag2,
  output [1:0] Selected_Set,
  output Evict_or_not
);

  wire [1:0] multiplexer_1_out, multiplexer_2_out;

  Multiplexer #(.width(2), .enable("false")) multiplexer_1 (
    .in0(2'b11), .in1(2'b00), .out(multiplexer_1_out), .sel(Tag0));
  Multiplexer #(.width(2), .enable("false")) multiplexer_2 (
    .in0(multiplexer_1_out), .in1(2'b01), .out(multiplexer_2_out), .sel(Tag1));
  Multiplexer #(.width(2), .enable("false")) multiplexer_3 (
    .in0(multiplexer_2_out), .in1(2'b10), .out(Selected_Set), .sel(Tag2));
  Comparator #(.width(2), .mode("unsigned")) comparator_1 (
    .a(Selected_Set), .b(2'b11), .eq(Evict_or_not));  // open: gt, lt

  // Other names for the same wires on the sheet: contains0 = Tag0; contains1 = Tag1; contains2 = Tag2;
  //   Evict = Evict_or_not; selectedTag[1:0] = Selected_Set
endmodule

module NextState (
  input  S2,
  input  S1,
  input  S0,
  input  C,
  input  V,
  input  D,
  input  R,
  input  W,
  output S2p,
  output S1p,
  output S0p,
  output Ready
);

  wire and_1_out, and_2_out, and_3_out, and_4_out, and_5_out, and_6_out, and_7_out, and_8_out, and_9_out,
       and_10_out, and_11_out, and_12_out, and_13_out, and_14_out, and_15_out, and_16_out, and_17_out,
       and_18_out, and_19_out, and_20_out, and_21_out, and_22_out, not_1_out, not_2_out, not_3_out,
       not_4_out, not_5_out, not_6_out, not_7_out, not_8_out, not_9_out, not_10_out, not_11_out, not_12_out,
       not_13_out, not_14_out, not_15_out, not_16_out, not_17_out, not_18_out, not_19_out, not_20_out,
       not_21_out, not_22_out, not_23_out, not_24_out, not_25_out, not_26_out, not_27_out, not_28_out,
       not_29_out, not_30_out, not_31_out, not_32_out, not_33_out, not_34_out, not_35_out, not_36_out,
       not_37_out;

  not not_1 (not_1_out, S1);
  not not_2 (not_2_out, S2);
  not not_3 (not_3_out, S2);
  not not_4 (not_4_out, V);
  not not_5 (not_5_out, S2);
  not not_6 (not_6_out, D);
  not not_7 (not_7_out, S2);
  not not_8 (not_8_out, R);
  not not_9 (not_9_out, W);
  not not_10 (not_10_out, S2);
  not not_11 (not_11_out, S1);
  not not_12 (not_12_out, S1);
  not not_13 (not_13_out, C);
  not not_14 (not_14_out, S1);
  not not_15 (not_15_out, C);
  not not_16 (not_16_out, S2);
  not not_17 (not_17_out, S0);
  not not_18 (not_18_out, S2);
  not not_19 (not_19_out, S0);
  not not_20 (not_20_out, S1);
  not not_21 (not_21_out, S2);
  not not_22 (not_22_out, S1);
  not not_23 (not_23_out, R);
  not not_24 (not_24_out, W);
  not not_25 (not_25_out, S1);
  not not_26 (not_26_out, S0);
  not not_27 (not_27_out, S0);
  not not_28 (not_28_out, S0);
  not not_29 (not_29_out, S2);
  not not_30 (not_30_out, S1);
  not not_31 (not_31_out, S2);
  not not_32 (not_32_out, S1);
  not not_33 (not_33_out, S0);
  not not_34 (not_34_out, S2);
  not not_35 (not_35_out, S1);
  not not_36 (not_36_out, R);
  not not_37 (not_37_out, W);
  and and_1 (and_1_out, not_1_out, S0, C, W);
  and and_2 (and_2_out, not_2_out, S0, C, R);
  and and_3 (and_3_out, not_3_out, S1, not_4_out);
  and and_4 (and_4_out, not_5_out, S1, not_6_out);
  and and_5 (and_5_out, not_7_out, S1, not_8_out, not_9_out);
  and and_6 (and_6_out, not_10_out, S1, S0);
  and and_7 (and_7_out, S2, not_11_out);
  and and_8 (and_8_out, not_12_out, S0, not_13_out, W);
  and and_9 (and_9_out, not_14_out, S0, not_15_out, R);
  and and_10 (and_10_out, not_16_out, S1, not_17_out, V, D, W);
  and and_11 (and_11_out, not_18_out, S1, not_19_out, V, D, R);
  and and_12 (and_12_out, S2, not_20_out, S0);
  and and_13 (and_13_out, not_21_out, not_22_out, not_23_out, not_24_out);
  and and_14 (and_14_out, not_25_out, not_26_out);
  and and_15 (and_15_out, not_27_out, V, D, W);
  and and_16 (and_16_out, not_28_out, V, D, R);
  and and_17 (and_17_out, not_29_out, not_30_out, C);
  and and_18 (and_18_out, S2, W);
  and and_19 (and_19_out, S2, S1);
  and and_20 (and_20_out, not_31_out, not_32_out, not_33_out);
  and and_21 (and_21_out, not_34_out, not_35_out, not_36_out, not_37_out);
  or or_1 (Ready, and_20_out, and_21_out, and_22_out);
  and and_22 (and_22_out, S2, S1);
  or or_2 (S2p, and_1_out, and_2_out, and_3_out, and_4_out, and_5_out, and_6_out, and_7_out);
  or or_3 (S1p, and_8_out, and_9_out, and_10_out, and_11_out, and_12_out);
  or or_4 (S0p, and_13_out, and_14_out, and_15_out, and_16_out, and_17_out, and_18_out, and_19_out);
endmodule

module ChooseOutputSignals (
  input  ReadFromMem,
  input  ReadReturn,
  input  WriteReturn,
  input  WriteToMem,
  input  [1:0] SelectedBlock,
  output ReadFromMem_2,
  output ReadReturn_2,
  output WriteReturn_2,
  output WriteToMem_2,
  output ReadFromMem_3,
  output ReadReturn_3,
  output WriteReturn_3,
  output WriteToMem_3,
  output ReadFromMem_4,
  output ReadReturn_4,
  output WriteReturn_4,
  output WriteToMem_4
);

  Multiplexer #(.select(2), .width(4), .enable("false")) multiplexer_1 (
    .in0({WriteToMem, WriteReturn, ReadReturn, ReadFromMem}), .in1(4'b0000), .in2(4'b0000), .in3(4'b0000),
    .out({WriteToMem_2, WriteReturn_2, ReadReturn_2, ReadFromMem_2}), .sel(SelectedBlock));
  Multiplexer #(.select(2), .width(4), .enable("false")) multiplexer_2 (
    .in0(4'b0000), .in1({WriteToMem, WriteReturn, ReadReturn, ReadFromMem}), .in2(4'b0000), .in3(4'b0000),
    .out({WriteToMem_3, WriteReturn_3, ReadReturn_3, ReadFromMem_3}), .sel(SelectedBlock));
  Multiplexer #(.select(2), .width(4), .enable("false")) multiplexer_3 (
    .in0(4'b0000), .in1(4'b0000), .in2({WriteToMem, WriteReturn, ReadReturn, ReadFromMem}), .in3(4'b0000),
    .out({WriteToMem_4, WriteReturn_4, ReadReturn_4, ReadFromMem_4}), .sel(SelectedBlock));

  // Other names for the same wires on the sheet: Signals[3:0] = {WriteToMem, WriteReturn, ReadReturn, ReadFromMem}
endmodule

module SetSelect (
  input  S2,
  input  S1,
  input  S0,
  input  Set,
  output S2_0,
  output S1_0,
  output S0_0,
  output S2_1,
  output S1_1,
  output S0_1
);

  wire or_1_out;
  wire [2:0] multiplexer_1_out;

  or or_1 (or_1_out, S2, S1, S0);
  Multiplexer #(.width(3), .enable("false")) multiplexer_1 (
    .in0(3'b000), .in1(3'b001), .out(multiplexer_1_out), .sel(or_1_out));
  Multiplexer #(.width(3), .enable("false")) multiplexer_2 (
    .in0({S2, S1, S0}), .in1(multiplexer_1_out), .out({S2_0, S1_0, S0_0}), .sel(Set));
  Multiplexer #(.width(3), .enable("false")) multiplexer_3 (
    .in0(multiplexer_1_out), .in1({S2, S1, S0}), .out({S2_1, S1_1, S0_1}), .sel(Set));

  // Other names for the same wires on the sheet: StartStates[2:0] = {S2, S1, S0}
endmodule

module SelectCVD (
  input  C0,
  input  V0,
  input  D0,
  input  C1,
  input  V1,
  input  D1,
  input  Set,
  output Contains,
  output Valid,
  output Dirty
);

  Multiplexer #(.enable("false")) multiplexer_1 (.in0(C0), .in1(C1), .out(Contains), .sel(Set));
  Multiplexer #(.enable("false")) multiplexer_2 (.in0(V0), .in1(V1), .out(Valid), .sel(Set));
  Multiplexer #(.enable("false")) multiplexer_3 (.in0(D0), .in1(D1), .out(Dirty), .sel(Set));

  // Other names for the same wires on the sheet: Contains_0 = C0; Contains_1 = C1; Dirty_0 = D0; Dirty_1 = D1;
  //   Valid_0 = V0; Valid_1 = V1
endmodule
